# Fritzing sketch PHMeter (saved by Fritzing 0.9.9b)

parts:
  U1 = NodeMCU V1.0
  WATER_PUMP1 = water pump/motor
  WATER_PUMP2 = water pump/motor
  KY-1 = Keyes Relay [package=THT]  # not connected
  LCD1 = LCD screen
  LCM1602_IIC2 = LCM1602 IIC [part_number="LCM1602 IIC" chip_label="LCM1602 IIC" package="DIP (Dual Inline) [THT]"]
  Part2 = MQ-3 breakout  # not connected
  U3 = ESP 32 DEVKIT DOIT  # not connected
  Part1 = ESP Base Board For NodeMCU Amica Lolin dan ESP32  # not connected

nets:
  N1: U1.D5, WATER_PUMP2.pin_2
  N2: U1.D6, WATER_PUMP1.pin_2
  N3: U1.GND, WATER_PUMP1.pin_1, WATER_PUMP2.pin_1
  VSS: LCD1.VSS, LCM1602_IIC2.VSS
  VDD: LCD1.VDD, LCM1602_IIC2.VDD
  N4: LCD1.V0, LCM1602_IIC2.V0
  N5: LCD1.RS, LCM1602_IIC2.RS
  N6: LCD1.R/W, LCM1602_IIC2.RW
  N7: LCD1.E, LCM1602_IIC2.E
  N8: LCD1.DB0, LCM1602_IIC2.D0
  N9: LCD1.DB1, LCM1602_IIC2.D1
  N10: LCD1.DB2, LCM1602_IIC2.D2
  N11: LCD1.DB3, LCM1602_IIC2.D3
  N12: LCD1.DB4, LCM1602_IIC2.D4
  N13: LCD1.DB5, LCM1602_IIC2.D5
  N14: LCD1.DB6, LCM1602_IIC2.D6
  N15: LCD1.DB7, LCM1602_IIC2.D7
  N16: LCD1.LED+, LCM1602_IIC2.A
  N17: LCD1.LED-, LCM1602_IIC2.K

custom parts:
  NodeMCU V1.0: ESP8266 based NodeMCU
  water pump/motor: WATER PUMP BY ARDUBLOCKTR
  Keyes Relay: The Keyes 5V relay module is suitable for SCM development, home appliance control. It uses a 5V~12V TIL control signal which can control DC / AC signal.
  LCM1602 IIC: I2C-Module to use a 1602 or 2004 LCD on with the wire.h libory Serial LCD Modul
  MQ-3 breakout: Alcohol sensor is capable of detecting alcohol (ethanol) particles on itself and gives the information in digital form back to us to manipulate with it. SKU:101251 • Voltage: 5V DC • Power: max 750mW • Measurement range: 0.04-4mg/L
